// Logisim project Control_Unit.circ as structural Verilog
module Control_Unit (
  input  START,
  input  FETCHED,
  input  RESET,
  input  [5:0] FuncCode,
  input  [5:0] OpCode,
  output fetch,
  output reset_2
);

  wire clk, demultiplexer_1_out0, demultiplexer_2_out0, demultiplexer_3_out0, demultiplexer_3_out1,
       demultiplexer_5_out0, demultiplexer_5_out1, END_q, EXEC_q, executed, FETCH_q, halt, IDLE_q, or_1_out,
       or_2_out, or_3_out, or_4_out, undriven;

  Clock clock_1 (.out(clk));
  or or_1 (or_1_out, demultiplexer_1_out0, 1'b1);
  Demultiplexer #(.enable("false")) demultiplexer_1 (
    .out0(demultiplexer_1_out0), .out1(fetch), .in(IDLE_q), .sel(START));
  D_Flip_Flop IDLE (.clk(or_1_out), .D(clk), .Q(IDLE_q), .preset(1'b1));  // open: Qn, en, reset
  or or_2 (or_2_out, demultiplexer_2_out0, demultiplexer_5_out1, fetch);
  D_Flip_Flop u_FETCH (.clk(or_2_out), .D(clk), .Q(FETCH_q), .preset(1'b1));  // open: Qn, en, reset
  Demultiplexer #(.enable("false")) demultiplexer_2 (
    .out0(demultiplexer_2_out0), .in(FETCH_q), .sel(FETCHED));  // open: out1
  // Switcher_CU switcher_cu_1: pin names not known; wires that end beside it: FuncCode, OpCode
  Demultiplexer #(.enable("false")) demultiplexer_3 (
    .out0(demultiplexer_3_out0), .out1(demultiplexer_3_out1), .sel(halt));  // open: in
  Demultiplexer #(.enable("false")) demultiplexer_4 (.sel(halt));  // open: out0, out1, in
  or or_3 (or_3_out, demultiplexer_5_out0, demultiplexer_3_out0);
  D_Flip_Flop EXEC (.clk(or_3_out), .D(clk), .Q(EXEC_q), .preset(undriven));  // open: Qn, en, reset
  Demultiplexer #(.enable("false")) demultiplexer_5 (
    .out0(demultiplexer_5_out0), .out1(demultiplexer_5_out1), .in(EXEC_q), .sel(executed));
  or or_4 (or_4_out, END_q, demultiplexer_3_out1);
  D_Flip_Flop END (.clk(or_4_out), .D(clk), .Q(END_q), .preset(undriven));  // open: Qn, en, reset

  assign reset_2 = RESET;

  // Other names for the same wires on the sheet: rst = RESET
endmodule
